# Fritzing sketch door lock fritzing (saved by Fritzing 0.9.10b)
circuit board: 8.46667cm x 5.64444cm
breadboards: 1

parts:
  Part1 = Arduino Mega ADK (Rev3)
  S1 = Square Pushbutton
  LED1 = RGB LED - (4 legs) [package="5 mm [THT]"]
  R1 = Resistor [tolerance=±5% resistance=220 package="2010 [SMD]"]
  R2 = Resistor [tolerance=±5% resistance=220 package="2010 [SMD]"]
  R3 = Resistor [tolerance=±5% resistance=220 package="2010 [SMD]"]
  LCD2 = LCD screen
  LCM1602_IIC2 = LCM1602 IIC [part_number="LCM1602 IIC" chip_label="LCM1602 IIC" package="DIP (Dual Inline) [THT]"]
  Part2 = Breadboard Power Supply Board SMD
  Part3 = IR Receiver Breakout [package=PCB]
  Keypad4x2 = Keypad Membran 4x4
  Part4 = RFID-RC522-v2
  J1 = Basic Servo

nets (from the breadboard view):
  N1: Part1.D21/SCL, LCM1602_IIC2.SCL
  N2: Part1.D20/SDA, LCM1602_IIC2.SDA
  N3: Part1.D13_PWM, Part3.OUT
  N4: Part1.D10_PWM, Keypad4x2.Pin5
  N5: Part1.D9_PWM, Keypad4x2.Pin1
  N6: Part1.D8_PWM, Keypad4x2.Pin2
  GND: Part1.GND, S1.leg0, LED1.common_anode, LCM1602_IIC2.GND, Part2.GND, Part3.GND, Part4.GND, J1.gnd
  N7: Part1.D2_PWM, Keypad4x2.Pin8
  N8: Part1.D3_PWM, Keypad4x2.Pin7
  N9: Part1.D4_PWM, Keypad4x2.Pin6
  N10: Part1.D5_PWM, Part4.RST
  N11: Part1.D6_PWM, Keypad4x2.Pin4
  N12: Part1.D7_PWM, Keypad4x2.Pin3
  N13: Part1.D32, S1.leg1
  N14: Part1.D34, R1.Pin_0
  N15: Part1.D36, R3.Pin_0
  N16: Part1.D38, R2.Pin_0
  N17: Part1.D50/MISO, Part4.MISO
  N18: Part1.D51/MOSI, Part4.MOSI
  N19: Part1.D52/SCK, Part4.SCK
  N20: Part1.D53/SS, Part4.SDA
  N21: LED1.red_cathode, R2.Pin_1
  N22: LED1.green_cathode, R3.Pin_1
  N23: LED1.blue_cathode, R1.Pin_1
  VSS: LCD2.VSS, LCM1602_IIC2.VSS
  VDD: LCD2.VDD, LCM1602_IIC2.VDD
  N24: LCD2.V0, LCM1602_IIC2.V0
  N25: LCD2.RS, LCM1602_IIC2.RS
  N26: LCD2.R/W, LCM1602_IIC2.RW
  N27: LCD2.E, LCM1602_IIC2.E
  N28: LCD2.DB0, LCM1602_IIC2.D0
  N29: LCD2.DB1, LCM1602_IIC2.D1
  N30: LCD2.DB2, LCM1602_IIC2.D2
  N31: LCD2.DB3, LCM1602_IIC2.D3
  N32: LCD2.DB4, LCM1602_IIC2.D4
  N33: LCD2.DB5, LCM1602_IIC2.D5
  N34: LCD2.DB6, LCM1602_IIC2.D6
  N35: LCD2.DB7, LCM1602_IIC2.D7
  N36: LCD2.LED+, LCM1602_IIC2.A
  N37: LCD2.LED-, LCM1602_IIC2.K
  VCC: LCM1602_IIC2.VCC, Part2.VCC, Part3.VCC, Part4.3_3V, J1.vcc
  N38: LCM1602_IIC2.LED_A, LCM1602_IIC2.LED_B

custom parts:
  LCM1602 IIC: I2C-Module to use a 1602 or 2004 LCD on with the wire.h libory Serial LCD Modul
  Keypad Membran 4x4: Membrane Keypad 4x4 Matrix
  RFID-RC522-v2: A simple China made RFID-RC522 Reader; do check the pin labels, as this is a MFRC522 based clone.
